// Digital circuit alu.dig as structural Verilog
module alu (
  input  [7:0] A,
  input  [2:0] S,
  input  [7:0] B,
  input  clk,
  input  Calc,
  input  Reg,
  input  Reg_2,
  output [7:0] out_4,
  output [7:0] out_5
);

  wire soma_8_bits_1_co, subtrator_8_bits_1_bo;
  wire [3:0] D1, D2, S1, S2;
  wire [7:0] A_t, AC, AUX, B_t, Divisao_1, Divisao_2, Multiplicacao_1, Multiplicacao_2, NAND, Shift_Direita,
       Shift_Esquerda, Soma_2, Subtracao_2, XOR;

  Register #(.Bits(8)) register_1 (.D(A), .C(clk), .en(Reg), .Q(A_t));
  Register #(.Bits(8)) register_2 (.D(B), .C(clk), .en(Reg_2), .Q(B_t));
  soma_8_bits soma_8_bits_1 (.A(A_t), .B(B_t), .S1(S1), .S2(S2), .Co(soma_8_bits_1_co));
  subtrator_8_bits subtrator_8_bits_1 (.A(A_t), .B(B_t), .D1(D1), .D2(D2), .Bo(subtrator_8_bits_1_bo));
  multiplicador_8_bits multiplicador_8_bits_1 (.A(A_t), .B(B_t), .LSB(Multiplicacao_1), .MSB(Multiplicacao_2));
  divisor_8_bits divisor_8_bits_1 (.D(A_t), .d_2(B_t), .MQ(Divisao_1), .AC(Divisao_2));
  shift_logico_esquerda shift_logico_esquerda_1 (.A(A_t), .S(Shift_Esquerda));
  shift_logico_direita shift_logico_direita_1 (.A(A_t), .S(Shift_Direita));
  nand2 nand2_1 (.A(A_t), .B(B_t), .S(NAND));
  xor2 xor2_1 (.A(A_t), .B(B_t), .S(XOR));
  BitExtender #(.inputBits(1), .outputBits(8)) bitextender_1 (.in(soma_8_bits_1_co), .out(Soma_2));
  BitExtender #(.inputBits(1), .outputBits(8)) bitextender_2 (.in(subtrator_8_bits_1_bo), .out(Subtracao_2));
  Multiplexer #(.Selector_Bits(3), .Bits(8)) multiplexer_1 (
    .sel(S), .in_0({S1, S2}), .in_1({D1, D2}), .in_2(Multiplicacao_1), .in_3(Divisao_1),
    .in_4(Shift_Esquerda), .in_5(Shift_Direita), .in_6(NAND), .in_7(XOR), .out(AC));
  Register #(.Bits(8)) register_3 (.D(AC), .C(clk), .en(Calc), .Q(out_4));
  Register #(.Bits(8)) register_4 (.D(AUX), .C(clk), .en(Calc), .Q(out_5));
  Multiplexer #(.Selector_Bits(3), .Bits(8)) multiplexer_2 (
    .sel(S), .in_0(Soma_2), .in_1(Subtracao_2), .in_2(Multiplicacao_2), .in_3(Divisao_2), .in_4({8{1'b0}}),
    .in_5({8{1'b0}}), .in_6({8{1'b0}}), .in_7({8{1'b0}}), .out(AUX));

  // Other names for the same wires on the sheet: Subtracao_1[7:0] = {D1, D2}; Q1[7:0] = out_4; Q2[7:0] = out_5;
  //   Soma_1[7:0] = {S1, S2}

  // Notes on the sheet:
  //   clk: Hz: 5
endmodule
