// Digital circuit divisor-8-bits.dig as structural Verilog
module divisor_8_bits (
  input  [7:0] D,
  input  [7:0] d_2,
  output [7:0] MQ,
  output [7:0] AC
);

  wire Cout0, Cout0_L2, Cout0_L3, Cout0_L4, Cout0_L5, Cout0_L6, Cout0_L7, Cout0_L8, Cout1, Cout1_L2,
       Cout1_L3, Cout1_L4, Cout1_L5, Cout1_L6, Cout1_L7, Cout1_L8, Cout2, Cout2_L2, Cout2_L3, Cout2_L4,
       Cout2_L5, Cout2_L6, Cout2_L7, Cout2_L8, Cout3, Cout3_L2, Cout3_L3, Cout3_L4, Cout3_L5, Cout3_L6,
       Cout3_L7, Cout3_L8, Cout4, Cout4_L2, Cout4_L3, Cout4_L4, Cout4_L5, Cout4_L6, Cout4_L7, Cout4_L8,
       Cout5, Cout5_L2, Cout5_L3, Cout5_L4, Cout5_L5, Cout5_L6, Cout5_L7, Cout5_L8, Cout6, Cout6_L2,
       Cout6_L3, Cout6_L4, Cout6_L5, Cout6_L6, Cout6_L7, Cout6_L8, R1_0, R1_1, R1_2, R1_3, R1_4, R1_5, R1_6,
       R1_7, R2_0, R2_1, R2_2, R2_3, R2_4, R2_5, R2_6, R2_7, R3_0, R3_1, R3_2, R3_3, R3_4, R3_5, R3_6, R3_7,
       R4_0, R4_1, R4_2, R4_3, R4_4, R4_5, R4_6, R4_7, R5_0, R5_1, R5_2, R5_3, R5_4, R5_5, R5_6, R5_7, R6_0,
       R6_1, R6_2, R6_3, R6_4, R6_5, R6_6, R6_7, R7_0, R7_1, R7_2, R7_3, R7_4, R7_5, R7_6, R7_7;

  sub_restore sub_restore_1 (.A(1'b0), .Cin(Cout6), .B(d_2[7]), .S(MQ[7]), .D(R1_7), .Cout(MQ[7]));
  sub_restore sub_restore_2 (.A(R1_6), .Cin(Cout6_L2), .B(d_2[7]), .S(MQ[6]), .D(R2_7), .Cout(MQ[6]));
  sub_restore sub_restore_3 (.A(R2_6), .Cin(Cout6_L3), .B(d_2[7]), .S(MQ[5]), .D(R3_7), .Cout(MQ[5]));
  sub_restore sub_restore_4 (.A(R3_6), .Cin(Cout6_L4), .B(d_2[7]), .S(MQ[4]), .D(R4_7), .Cout(MQ[4]));
  sub_restore sub_restore_5 (.A(R4_6), .Cin(Cout6_L5), .B(d_2[7]), .S(MQ[3]), .D(R5_7), .Cout(MQ[3]));
  sub_restore sub_restore_6 (.A(R5_6), .Cin(Cout6_L6), .B(d_2[7]), .S(MQ[2]), .D(R6_7), .Cout(MQ[2]));
  sub_restore sub_restore_7 (.A(R6_6), .Cin(Cout6_L7), .B(d_2[7]), .S(MQ[1]), .D(R7_7), .Cout(MQ[1]));
  sub_restore sub_restore_8 (.A(R7_6), .Cin(Cout6_L8), .B(d_2[7]), .S(MQ[0]), .D(AC[7]), .Cout(MQ[0]));
  sub_restore sub_restore_9 (.A(1'b0), .Cin(Cout5), .B(d_2[6]), .S(MQ[7]), .D(R1_6), .Cout(Cout6));
  sub_restore sub_restore_10 (.A(R1_5), .Cin(Cout5_L2), .B(d_2[6]), .S(MQ[6]), .D(R2_6), .Cout(Cout6_L2));
  sub_restore sub_restore_11 (.A(R2_5), .Cin(Cout5_L3), .B(d_2[6]), .S(MQ[5]), .D(R3_6), .Cout(Cout6_L3));
  sub_restore sub_restore_12 (.A(R3_5), .Cin(Cout5_L4), .B(d_2[6]), .S(MQ[4]), .D(R4_6), .Cout(Cout6_L4));
  sub_restore sub_restore_13 (.A(R4_5), .Cin(Cout5_L5), .B(d_2[6]), .S(MQ[3]), .D(R5_6), .Cout(Cout6_L5));
  sub_restore sub_restore_14 (.A(R5_5), .Cin(Cout5_L6), .B(d_2[6]), .S(MQ[2]), .D(R6_6), .Cout(Cout6_L6));
  sub_restore sub_restore_15 (.A(R6_5), .Cin(Cout5_L7), .B(d_2[6]), .S(MQ[1]), .D(R7_6), .Cout(Cout6_L7));
  sub_restore sub_restore_16 (.A(R7_5), .Cin(Cout5_L8), .B(d_2[6]), .S(MQ[0]), .D(AC[6]), .Cout(Cout6_L8));
  sub_restore sub_restore_17 (.A(1'b0), .Cin(Cout4), .B(d_2[5]), .S(MQ[7]), .D(R1_5), .Cout(Cout5));
  sub_restore sub_restore_18 (.A(R1_4), .Cin(Cout4_L2), .B(d_2[5]), .S(MQ[6]), .D(R2_5), .Cout(Cout5_L2));
  sub_restore sub_restore_19 (.A(R2_4), .Cin(Cout4_L3), .B(d_2[5]), .S(MQ[5]), .D(R3_5), .Cout(Cout5_L3));
  sub_restore sub_restore_20 (.A(R3_4), .Cin(Cout4_L4), .B(d_2[5]), .S(MQ[4]), .D(R4_5), .Cout(Cout5_L4));
  sub_restore sub_restore_21 (.A(R4_4), .Cin(Cout4_L5), .B(d_2[5]), .S(MQ[3]), .D(R5_5), .Cout(Cout5_L5));
  sub_restore sub_restore_22 (.A(R5_4), .Cin(Cout4_L6), .B(d_2[5]), .S(MQ[2]), .D(R6_5), .Cout(Cout5_L6));
  sub_restore sub_restore_23 (.A(R6_4), .Cin(Cout4_L7), .B(d_2[5]), .S(MQ[1]), .D(R7_5), .Cout(Cout5_L7));
  sub_restore sub_restore_24 (.A(R7_4), .Cin(Cout4_L8), .B(d_2[5]), .S(MQ[0]), .D(AC[5]), .Cout(Cout5_L8));
  sub_restore sub_restore_25 (.A(1'b0), .Cin(Cout3), .B(d_2[4]), .S(MQ[7]), .D(R1_4), .Cout(Cout4));
  sub_restore sub_restore_26 (.A(R1_3), .Cin(Cout3_L2), .B(d_2[4]), .S(MQ[6]), .D(R2_4), .Cout(Cout4_L2));
  sub_restore sub_restore_27 (.A(R2_3), .Cin(Cout3_L3), .B(d_2[4]), .S(MQ[5]), .D(R3_4), .Cout(Cout4_L3));
  sub_restore sub_restore_28 (.A(R3_3), .Cin(Cout3_L4), .B(d_2[4]), .S(MQ[4]), .D(R4_4), .Cout(Cout4_L4));
  sub_restore sub_restore_29 (.A(R4_3), .Cin(Cout3_L5), .B(d_2[4]), .S(MQ[3]), .D(R5_4), .Cout(Cout4_L5));
  sub_restore sub_restore_30 (.A(R5_3), .Cin(Cout3_L6), .B(d_2[4]), .S(MQ[2]), .D(R6_4), .Cout(Cout4_L6));
  sub_restore sub_restore_31 (.A(R6_3), .Cin(Cout3_L7), .B(d_2[4]), .S(MQ[1]), .D(R7_4), .Cout(Cout4_L7));
  sub_restore sub_restore_32 (.A(R7_3), .Cin(Cout3_L8), .B(d_2[4]), .S(MQ[0]), .D(AC[4]), .Cout(Cout4_L8));
  sub_restore sub_restore_33 (.A(1'b0), .Cin(Cout2), .B(d_2[3]), .S(MQ[7]), .D(R1_3), .Cout(Cout3));
  sub_restore sub_restore_34 (.A(R1_2), .Cin(Cout2_L2), .B(d_2[3]), .S(MQ[6]), .D(R2_3), .Cout(Cout3_L2));
  sub_restore sub_restore_35 (.A(R2_2), .Cin(Cout2_L3), .B(d_2[3]), .S(MQ[5]), .D(R3_3), .Cout(Cout3_L3));
  sub_restore sub_restore_36 (.A(R3_2), .Cin(Cout2_L4), .B(d_2[3]), .S(MQ[4]), .D(R4_3), .Cout(Cout3_L4));
  sub_restore sub_restore_37 (.A(R4_2), .Cin(Cout2_L5), .B(d_2[3]), .S(MQ[3]), .D(R5_3), .Cout(Cout3_L5));
  sub_restore sub_restore_38 (.A(R5_2), .Cin(Cout2_L6), .B(d_2[3]), .S(MQ[2]), .D(R6_3), .Cout(Cout3_L6));
  sub_restore sub_restore_39 (.A(R6_2), .Cin(Cout2_L7), .B(d_2[3]), .S(MQ[1]), .D(R7_3), .Cout(Cout3_L7));
  sub_restore sub_restore_40 (.A(R7_2), .Cin(Cout2_L8), .B(d_2[3]), .S(MQ[0]), .D(AC[3]), .Cout(Cout3_L8));
  sub_restore sub_restore_41 (.A(1'b0), .Cin(Cout1), .B(d_2[2]), .S(MQ[7]), .D(R1_2), .Cout(Cout2));
  sub_restore sub_restore_42 (.A(R1_1), .Cin(Cout1_L2), .B(d_2[2]), .S(MQ[6]), .D(R2_2), .Cout(Cout2_L2));
  sub_restore sub_restore_43 (.A(R2_1), .Cin(Cout1_L3), .B(d_2[2]), .S(MQ[5]), .D(R3_2), .Cout(Cout2_L3));
  sub_restore sub_restore_44 (.A(R3_1), .Cin(Cout1_L4), .B(d_2[2]), .S(MQ[4]), .D(R4_2), .Cout(Cout2_L4));
  sub_restore sub_restore_45 (.A(R4_1), .Cin(Cout1_L5), .B(d_2[2]), .S(MQ[3]), .D(R5_2), .Cout(Cout2_L5));
  sub_restore sub_restore_46 (.A(R5_1), .Cin(Cout1_L6), .B(d_2[2]), .S(MQ[2]), .D(R6_2), .Cout(Cout2_L6));
  sub_restore sub_restore_47 (.A(R6_1), .Cin(Cout1_L7), .B(d_2[2]), .S(MQ[1]), .D(R7_2), .Cout(Cout2_L7));
  sub_restore sub_restore_48 (.A(R7_1), .Cin(Cout1_L8), .B(d_2[2]), .S(MQ[0]), .D(AC[2]), .Cout(Cout2_L8));
  sub_restore sub_restore_49 (.A(1'b0), .Cin(Cout0), .B(d_2[1]), .S(MQ[7]), .D(R1_1), .Cout(Cout1));
  sub_restore sub_restore_50 (.A(R1_0), .Cin(Cout0_L2), .B(d_2[1]), .S(MQ[6]), .D(R2_1), .Cout(Cout1_L2));
  sub_restore sub_restore_51 (.A(R2_0), .Cin(Cout0_L3), .B(d_2[1]), .S(MQ[5]), .D(R3_1), .Cout(Cout1_L3));
  sub_restore sub_restore_52 (.A(R3_0), .Cin(Cout0_L4), .B(d_2[1]), .S(MQ[4]), .D(R4_1), .Cout(Cout1_L4));
  sub_restore sub_restore_53 (.A(R4_0), .Cin(Cout0_L5), .B(d_2[1]), .S(MQ[3]), .D(R5_1), .Cout(Cout1_L5));
  sub_restore sub_restore_54 (.A(R5_0), .Cin(Cout0_L6), .B(d_2[1]), .S(MQ[2]), .D(R6_1), .Cout(Cout1_L6));
  sub_restore sub_restore_55 (.A(R6_0), .Cin(Cout0_L7), .B(d_2[1]), .S(MQ[1]), .D(R7_1), .Cout(Cout1_L7));
  sub_restore sub_restore_56 (.A(R7_0), .Cin(Cout0_L8), .B(d_2[1]), .S(MQ[0]), .D(AC[1]), .Cout(Cout1_L8));
  sub_restore sub_restore_57 (.A(D[7]), .Cin(1'b1), .B(d_2[0]), .S(MQ[7]), .D(R1_0), .Cout(Cout0));
  sub_restore sub_restore_58 (.A(D[6]), .Cin(1'b1), .B(d_2[0]), .S(MQ[6]), .D(R2_0), .Cout(Cout0_L2));
  sub_restore sub_restore_59 (.A(D[5]), .Cin(1'b1), .B(d_2[0]), .S(MQ[5]), .D(R3_0), .Cout(Cout0_L3));
  sub_restore sub_restore_60 (.A(D[4]), .Cin(1'b1), .B(d_2[0]), .S(MQ[4]), .D(R4_0), .Cout(Cout0_L4));
  sub_restore sub_restore_61 (.A(D[3]), .Cin(1'b1), .B(d_2[0]), .S(MQ[3]), .D(R5_0), .Cout(Cout0_L5));
  sub_restore sub_restore_62 (.A(D[2]), .Cin(1'b1), .B(d_2[0]), .S(MQ[2]), .D(R6_0), .Cout(Cout0_L6));
  sub_restore sub_restore_63 (.A(D[1]), .Cin(1'b1), .B(d_2[0]), .S(MQ[1]), .D(R7_0), .Cout(Cout0_L7));
  sub_restore sub_restore_64 (.A(D[0]), .Cin(1'b1), .B(d_2[0]), .S(MQ[0]), .D(AC[0]), .Cout(Cout0_L8));

  // Other names for the same wires on the sheet: Cout7_L1 = MQ[7]; Cout7_L2 = MQ[6]; Cout7_L3 = MQ[5];
  //   Cout7_L4 = MQ[4]; Cout7_L5 = MQ[3]; Cout7_L6 = MQ[2]; Cout7_L7 = MQ[1]; Cout7_L8 = MQ[0]; d0_t = d_2[0];
  //   d1_t = d_2[1]; d2_t = d_2[2]; d3_t = d_2[3]; d4_t = d_2[4]; d5_t = d_2[5]; d6_t = d_2[6]; d7_t = d_2[7];
  //   R8_0 = AC[0]; R8_1 = AC[1]; R8_2 = AC[2]; R8_3 = AC[3]; R8_4 = AC[4]; R8_5 = AC[5]; R8_6 = AC[6]; R8_7 = AC[7]
endmodule
