// Digital circuit multiplicador-8-bits.dig as structural Verilog
module multiplicador_8_bits (
  input  [7:0] A,
  input  [7:0] B,
  output [7:0] LSB,
  output [7:0] MSB
);

  wire A0B1, A0B2, A0B3, A0B4, A0B5, A0B6, A0B7, A1B0, A1B1, A1B2, A1B3, A1B4, A1B5, A1B6, A1B7, A2B0, A2B1,
       A2B2, A2B3, A2B4, A2B5, A2B6, A2B7, A3B0, A3B1, A3B2, A3B3, A3B4, A3B5, A3B6, A3B7, A4B0, A4B1, A4B2,
       A4B3, A4B4, A4B5, A4B6, A4B7, A5B0, A5B1, A5B2, A5B3, A5B4, A5B5, A5B6, A5B7, A6B0, A6B1, A6B2, A6B3,
       A6B4, A6B5, A6B6, A6B7, A7B0, A7B1, A7B2, A7B3, A7B4, A7B5, A7B6, A7B7, Co0, Co1, Co2, Co3, Co4, Co5,
       Co6, Co7, Co8, Co9, Co10, Co11, Co12, Co13, Co14, Co15, Co16, Co17, Co18, Co19, Co20, Co21, Co22,
       Co23, Co24, Co25, Co26, Co27, Co28, Co29, Co30, Co31, Co32, Co33, Co34, Co35, Co36, Co37, Co38, Co39,
       Co40, Co41, Co42, Co43, Co44, Co45, Co46, Co47, Co48, Co49, Co50, Co51, Co52, Co53, Co54, SS2, SS3,
       SS4, SS5, SS6, SS7, SS8, SS9, SS10, SS11, SS12, SS13, SSS3, SSS4, SSS5, SSS6, SSS7, SSS8, SSS9, SSS10,
       SSS11, SSS12, SSSS4, SSSS5, SSSS6, SSSS7, SSSS8, SSSS9, SSSS10, SSSS11, SSSSS5, SSSSS6, SSSSS7,
       SSSSS8, SSSSS9, SSSSS10, SSSSSS6, SSSSSS7, SSSSSS8, SSSSSS9, SSSSSSS7, SSSSSSS8;

  and and_1 (LSB[0], A[0], B[0]);
  and and_2 (A0B1, A[0], B[1]);
  and and_3 (A0B2, A[0], B[2]);
  and and_4 (A0B3, A[0], B[3]);
  and and_5 (A0B4, A[0], B[4]);
  and and_6 (A0B5, A[0], B[5]);
  and and_7 (A0B6, A[0], B[6]);
  and and_8 (A0B7, A[0], B[7]);
  and and_9 (A1B0, A[1], B[0]);
  and and_10 (A1B1, A[1], B[1]);
  and and_11 (A1B2, A[1], B[2]);
  and and_12 (A1B3, A[1], B[3]);
  and and_13 (A1B4, A[1], B[4]);
  and and_14 (A1B5, A[1], B[5]);
  and and_15 (A1B6, A[1], B[6]);
  and and_16 (A1B7, A[1], B[7]);
  soma_1_bit soma_1_bit_1 (.A(A0B1), .B(A1B0), .Ci(1'b0), .S(LSB[1]), .Co(Co0));
  and and_17 (A2B0, A[2], B[0]);
  and and_18 (A2B1, A[2], B[1]);
  and and_19 (A2B2, A[2], B[2]);
  and and_20 (A2B3, A[2], B[3]);
  and and_21 (A2B4, A[2], B[4]);
  and and_22 (A2B5, A[2], B[5]);
  and and_23 (A2B6, A[2], B[6]);
  and and_24 (A2B7, A[2], B[7]);
  soma_1_bit soma_1_bit_2 (.A(A0B2), .B(A1B1), .Ci(Co0), .S(SS2), .Co(Co1));
  soma_1_bit soma_1_bit_3 (.A(SS2), .B(A2B0), .Ci(1'b0), .S(LSB[2]), .Co(Co2));
  and and_25 (A3B0, A[3], B[0]);
  and and_26 (A3B1, A[3], B[1]);
  and and_27 (A3B2, A[3], B[2]);
  and and_28 (A3B3, A[3], B[3]);
  and and_29 (A3B4, A[3], B[4]);
  and and_30 (A3B5, A[3], B[5]);
  and and_31 (A3B6, A[3], B[6]);
  and and_32 (A3B7, A[3], B[7]);
  soma_1_bit soma_1_bit_4 (.A(A0B3), .B(A1B2), .Ci(Co1), .S(SS3), .Co(Co3));
  soma_1_bit soma_1_bit_5 (.A(SS3), .B(A2B1), .Ci(Co2), .S(SSS3), .Co(Co4));
  soma_1_bit soma_1_bit_6 (.A(SSS3), .B(A3B0), .Ci(1'b0), .S(LSB[3]), .Co(Co5));
  and and_33 (A4B0, A[4], B[0]);
  and and_34 (A4B1, A[4], B[1]);
  and and_35 (A4B2, A[4], B[2]);
  and and_36 (A4B3, A[4], B[3]);
  and and_37 (A4B4, A[4], B[4]);
  and and_38 (A4B5, A[4], B[5]);
  and and_39 (A4B6, A[4], B[6]);
  and and_40 (A4B7, A[4], B[7]);
  soma_1_bit soma_1_bit_7 (.A(A0B4), .B(A1B3), .Ci(Co3), .S(SS4), .Co(Co6));
  soma_1_bit soma_1_bit_8 (.A(SS4), .B(A2B2), .Ci(Co4), .S(SSS4), .Co(Co7));
  soma_1_bit soma_1_bit_9 (.A(SSS4), .B(A3B1), .Ci(Co5), .S(SSSS4), .Co(Co8));
  soma_1_bit soma_1_bit_10 (.A(SSSS4), .B(A4B0), .Ci(1'b0), .S(LSB[4]), .Co(Co9));
  and and_41 (A5B0, A[5], B[0]);
  and and_42 (A5B1, A[5], B[1]);
  and and_43 (A5B2, A[5], B[2]);
  and and_44 (A5B3, A[5], B[3]);
  and and_45 (A5B4, A[5], B[4]);
  and and_46 (A5B5, A[5], B[5]);
  and and_47 (A5B6, A[5], B[6]);
  and and_48 (A5B7, A[5], B[7]);
  soma_1_bit soma_1_bit_11 (.A(A0B5), .B(A1B4), .Ci(Co6), .S(SS5), .Co(Co10));
  soma_1_bit soma_1_bit_12 (.A(SS5), .B(A2B3), .Ci(Co7), .S(SSS5), .Co(Co11));
  soma_1_bit soma_1_bit_13 (.A(SSS5), .B(A3B2), .Ci(Co8), .S(SSSS5), .Co(Co12));
  soma_1_bit soma_1_bit_14 (.A(SSSS5), .B(A4B1), .Ci(Co9), .S(SSSSS5), .Co(Co13));
  soma_1_bit soma_1_bit_15 (.A(SSSSS5), .B(A5B0), .Ci(1'b0), .S(LSB[5]), .Co(Co14));
  and and_49 (A6B0, A[6], B[0]);
  and and_50 (A6B1, A[6], B[1]);
  and and_51 (A6B2, A[6], B[2]);
  and and_52 (A6B3, A[6], B[3]);
  and and_53 (A6B4, A[6], B[4]);
  and and_54 (A6B5, A[6], B[5]);
  and and_55 (A6B6, A[6], B[6]);
  and and_56 (A6B7, A[6], B[7]);
  soma_1_bit soma_1_bit_16 (.A(A0B6), .B(A1B5), .Ci(Co10), .S(SS6), .Co(Co15));
  soma_1_bit soma_1_bit_17 (.A(SS6), .B(A2B4), .Ci(Co11), .S(SSS6), .Co(Co16));
  soma_1_bit soma_1_bit_18 (.A(SSS6), .B(A3B3), .Ci(Co12), .S(SSSS6), .Co(Co17));
  soma_1_bit soma_1_bit_19 (.A(SSSS6), .B(A4B2), .Ci(Co13), .S(SSSSS6), .Co(Co18));
  soma_1_bit soma_1_bit_20 (.A(SSSSS6), .B(A5B1), .Ci(Co14), .S(SSSSSS6), .Co(Co19));
  soma_1_bit soma_1_bit_21 (.A(SSSSSS6), .B(A6B0), .Ci(1'b0), .S(LSB[6]), .Co(Co20));
  and and_57 (A7B0, A[7], B[0]);
  and and_58 (A7B1, A[7], B[1]);
  and and_59 (A7B2, A[7], B[2]);
  and and_60 (A7B3, A[7], B[3]);
  and and_61 (A7B4, A[7], B[4]);
  and and_62 (A7B5, A[7], B[5]);
  and and_63 (A7B6, A[7], B[6]);
  and and_64 (A7B7, A[7], B[7]);
  soma_1_bit soma_1_bit_22 (.A(A0B7), .B(A1B6), .Ci(Co15), .S(SS7), .Co(Co21));
  soma_1_bit soma_1_bit_23 (.A(SS7), .B(A2B5), .Ci(Co16), .S(SSS7), .Co(Co22));
  soma_1_bit soma_1_bit_24 (.A(SSS7), .B(A3B4), .Ci(Co17), .S(SSSS7), .Co(Co23));
  soma_1_bit soma_1_bit_25 (.A(SSSS7), .B(A4B3), .Ci(Co18), .S(SSSSS7), .Co(Co24));
  soma_1_bit soma_1_bit_26 (.A(SSSSS7), .B(A5B2), .Ci(Co19), .S(SSSSSS7), .Co(Co25));
  soma_1_bit soma_1_bit_27 (.A(SSSSSS7), .B(A6B1), .Ci(Co20), .S(SSSSSSS7), .Co(Co26));
  soma_1_bit soma_1_bit_28 (.A(SSSSSSS7), .B(A7B0), .Ci(1'b0), .S(LSB[7]), .Co(Co27));
  soma_1_bit soma_1_bit_29 (.A(A1B7), .B(Co21), .Ci(1'b0), .S(SS8), .Co(Co28));
  soma_1_bit soma_1_bit_30 (.A(SS8), .B(A2B6), .Ci(Co22), .S(SSS8), .Co(Co29));
  soma_1_bit soma_1_bit_31 (.A(SSS8), .B(A3B5), .Ci(Co23), .S(SSSS8), .Co(Co30));
  soma_1_bit soma_1_bit_32 (.A(SSSS8), .B(A4B4), .Ci(Co24), .S(SSSSS8), .Co(Co31));
  soma_1_bit soma_1_bit_33 (.A(SSSSS8), .B(A5B3), .Ci(Co25), .S(SSSSSS8), .Co(Co32));
  soma_1_bit soma_1_bit_34 (.A(SSSSSS8), .B(A6B2), .Ci(Co26), .S(SSSSSSS8), .Co(Co33));
  soma_1_bit soma_1_bit_35 (.A(SSSSSSS8), .B(A7B1), .Ci(Co27), .S(MSB[0]), .Co(Co34));
  soma_1_bit soma_1_bit_36 (.A(A2B7), .B(Co28), .Ci(Co29), .S(SS9), .Co(Co35));
  soma_1_bit soma_1_bit_37 (.A(A3B6), .B(SS9), .Ci(Co30), .S(SSS9), .Co(Co36));
  soma_1_bit soma_1_bit_38 (.A(A4B5), .B(SSS9), .Ci(Co31), .S(SSSS9), .Co(Co37));
  soma_1_bit soma_1_bit_39 (.A(A5B4), .B(SSSS9), .Ci(Co32), .S(SSSSS9), .Co(Co38));
  soma_1_bit soma_1_bit_40 (.A(A6B3), .B(SSSSS9), .Ci(Co33), .S(SSSSSS9), .Co(Co39));
  soma_1_bit soma_1_bit_41 (.A(A7B2), .B(SSSSSS9), .Ci(Co34), .S(MSB[1]), .Co(Co40));
  soma_1_bit soma_1_bit_42 (.A(A3B7), .B(Co35), .Ci(Co36), .S(SS10), .Co(Co41));
  soma_1_bit soma_1_bit_43 (.A(A4B6), .B(SS10), .Ci(Co37), .S(SSS10), .Co(Co42));
  soma_1_bit soma_1_bit_44 (.A(A5B5), .B(SSS10), .Ci(Co38), .S(SSSS10), .Co(Co43));
  soma_1_bit soma_1_bit_45 (.A(A6B4), .B(SSSS10), .Ci(Co39), .S(SSSSS10), .Co(Co44));
  soma_1_bit soma_1_bit_46 (.A(A7B3), .B(SSSSS10), .Ci(Co40), .S(MSB[2]), .Co(Co45));
  soma_1_bit soma_1_bit_47 (.A(A4B7), .B(Co41), .Ci(Co42), .S(SS11), .Co(Co46));
  soma_1_bit soma_1_bit_48 (.A(A5B6), .B(SS11), .Ci(Co43), .S(SSS11), .Co(Co47));
  soma_1_bit soma_1_bit_49 (.A(A6B5), .B(SSS11), .Ci(Co44), .S(SSSS11), .Co(Co48));
  soma_1_bit soma_1_bit_50 (.A(A7B4), .B(SSSS11), .Ci(Co45), .S(MSB[3]), .Co(Co49));
  soma_1_bit soma_1_bit_51 (.A(A5B7), .B(Co46), .Ci(Co47), .S(SS12), .Co(Co50));
  soma_1_bit soma_1_bit_52 (.A(A6B6), .B(SS12), .Ci(Co48), .S(SSS12), .Co(Co51));
  soma_1_bit soma_1_bit_53 (.A(A7B5), .B(SSS12), .Ci(Co49), .S(MSB[4]), .Co(Co52));
  soma_1_bit soma_1_bit_54 (.A(A6B7), .B(Co50), .Ci(Co51), .S(SS13), .Co(Co53));
  soma_1_bit soma_1_bit_55 (.A(A7B6), .B(SS13), .Ci(Co52), .S(MSB[5]), .Co(Co54));
  soma_1_bit soma_1_bit_56 (.A(A7B7), .B(Co53), .Ci(Co54), .S(MSB[6]), .Co(MSB[7]));

  // Other names for the same wires on the sheet: S0 = LSB[0]; S1 = LSB[1]; S2 = LSB[2]; S3 = LSB[3]; S4 = LSB[4];
  //   S5 = LSB[5]; S6 = LSB[6]; S7 = LSB[7]; S8 = MSB[0]; S9 = MSB[1]; S10 = MSB[2]; S11 = MSB[3]; S12 = MSB[4];
  //   S13 = MSB[5]; S14 = MSB[6]; S15 = MSB[7]
endmodule
