// Digital circuit soma-8-bits.dig as structural Verilog
module soma_8_bits (
  input  [7:0] A,
  input  [7:0] B,
  output [3:0] S1,
  output [3:0] S2,
  output Co
);

  wire soma_1_bit_1_co, soma_1_bit_2_co, soma_1_bit_3_co, soma_1_bit_4_co, soma_1_bit_5_co, soma_1_bit_6_co,
       soma_1_bit_7_co;

  soma_1_bit soma_1_bit_1 (.A(A[0]), .B(B[0]), .Ci(1'b0), .S(S2[0]), .Co(soma_1_bit_1_co));
  soma_1_bit soma_1_bit_2 (.A(A[1]), .B(B[1]), .Ci(soma_1_bit_1_co), .S(S2[1]), .Co(soma_1_bit_2_co));
  soma_1_bit soma_1_bit_3 (.A(A[2]), .B(B[2]), .Ci(soma_1_bit_2_co), .S(S2[2]), .Co(soma_1_bit_3_co));
  soma_1_bit soma_1_bit_4 (.A(A[3]), .B(B[3]), .Ci(soma_1_bit_3_co), .S(S2[3]), .Co(soma_1_bit_4_co));
  soma_1_bit soma_1_bit_5 (.A(A[4]), .B(B[4]), .Ci(soma_1_bit_4_co), .S(S1[0]), .Co(soma_1_bit_5_co));
  soma_1_bit soma_1_bit_6 (.A(A[5]), .B(B[5]), .Ci(soma_1_bit_5_co), .S(S1[1]), .Co(soma_1_bit_6_co));
  soma_1_bit soma_1_bit_7 (.A(A[6]), .B(B[6]), .Ci(soma_1_bit_6_co), .S(S1[2]), .Co(soma_1_bit_7_co));
  soma_1_bit soma_1_bit_8 (.A(A[7]), .B(B[7]), .Ci(soma_1_bit_7_co), .S(S1[3]), .Co(Co));

  // Other names for the same wires on the sheet: S0 = S2[0]; S1_t = S2[1]; S2_t = S2[2]; S3 = S2[3]; S4 = S1[0];
  //   S5 = S1[1]; S6 = S1[2]; S7 = S1[3]
endmodule
