// Digital circuit sub-restore.dig as structural Verilog
module sub_restore (
  input  A,
  input  Cin,
  input  B,
  input  S,
  output D,
  output Cout
);

  wire B_t, D_t;

  not not_1 (B_t, B);
  soma_1_bit soma_1_bit_1 (.A(A), .B(B_t), .Ci(Cin), .S(D_t), .Co(Cout));
  Multiplexer multiplexer_1 (.sel(S), .in_0(A), .in_1(D_t), .out(D));
endmodule
