// Digital circuit subtrator-1-bit.dig as structural Verilog
module subtrator_1_bit (
  input  B,
  input  A,
  input  Cin,
  output D,
  output Cout
);

  wire and_1_out, and_2_out, and_3_out, not_1_out, not_2_out;

  xor xor_1 (D, A, B, Cin);
  and and_1 (and_1_out, not_1_out, A);
  not not_1 (not_1_out, B);
  and and_2 (and_2_out, not_2_out, Cin);
  not not_2 (not_2_out, B);
  and and_3 (and_3_out, A, Cin);
  or or_1 (Cout, and_1_out, and_2_out, and_3_out);
endmodule
