// Digital circuit subtrator-8-bits.dig as structural Verilog
module subtrator_8_bits (
  input  [7:0] A,
  input  [7:0] B,
  output [3:0] D1,
  output [3:0] D2,
  output Bo
);

  wire subtrator_1_bit_1_cout, subtrator_1_bit_2_cout, subtrator_1_bit_3_cout, subtrator_1_bit_4_cout,
       subtrator_1_bit_5_cout, subtrator_1_bit_6_cout, subtrator_1_bit_7_cout;

  subtrator_1_bit subtrator_1_bit_1 (.B(A[0]), .A(B[0]), .Cin(1'b0), .D(D2[0]), .Cout(subtrator_1_bit_1_cout));
  subtrator_1_bit subtrator_1_bit_2 (
    .B(A[1]), .A(B[1]), .Cin(subtrator_1_bit_1_cout), .D(D2[1]), .Cout(subtrator_1_bit_2_cout));
  subtrator_1_bit subtrator_1_bit_3 (
    .B(A[2]), .A(B[2]), .Cin(subtrator_1_bit_2_cout), .D(D2[2]), .Cout(subtrator_1_bit_3_cout));
  subtrator_1_bit subtrator_1_bit_4 (
    .B(A[3]), .A(B[3]), .Cin(subtrator_1_bit_3_cout), .D(D2[3]), .Cout(subtrator_1_bit_4_cout));
  subtrator_1_bit subtrator_1_bit_5 (
    .B(A[4]), .A(B[4]), .Cin(subtrator_1_bit_4_cout), .D(D1[0]), .Cout(subtrator_1_bit_5_cout));
  subtrator_1_bit subtrator_1_bit_6 (
    .B(A[5]), .A(B[5]), .Cin(subtrator_1_bit_5_cout), .D(D1[1]), .Cout(subtrator_1_bit_6_cout));
  subtrator_1_bit subtrator_1_bit_7 (
    .B(A[6]), .A(B[6]), .Cin(subtrator_1_bit_6_cout), .D(D1[2]), .Cout(subtrator_1_bit_7_cout));
  subtrator_1_bit subtrator_1_bit_8 (.B(A[7]), .A(B[7]), .Cin(subtrator_1_bit_7_cout), .D(D1[3]), .Cout(Bo));

  // Other names for the same wires on the sheet: D0 = D2[0]; D1_t = D2[1]; D2_t = D2[2]; D3 = D2[3]; D4 = D1[0];
  //   D5 = D1[1]; D6 = D1[2]; D7 = D1[3]
endmodule
